# Fritzing sketch Sketch (saved by Fritzing 0.9.3b)
breadboards: 1

parts:
  Часть1 = Arduino Uno (Rev3)
  GLCD_128x1 = 128 x 64 Graphic LCD  # not connected
  S1 = SWITCH-MOMENTARY-2 [package=tactile-pth]  # not connected
  S2 = SWITCH-MOMENTARY-2 [package=tactile-pth]  # not connected
  S3 = SWITCH-MOMENTARY-2 [package=tactile-pth]  # not connected
  S4 = SWITCH-MOMENTARY-2 [package=tactile-pth]  # not connected
  Часть2 = BME280
  M1 = ph-4502c [package=THT]
  Capacitive_Soil_Moisture_Sensor1 = Capacitive Soil Moisture Sensor V2.0
  IC1 = ADS1115 16-bit ADC Breakout  # not connected
  Espessif_Serial_Wifi_Modul_1 = ESP8266 ESP01 [part_number=ESP8266 package=THT]
  S5 = LDR light sensor [package=THT]

nets:
  VCC: Часть1.5V, Часть2.VIN, M1.pin6, Capacitive_Soil_Moisture_Sensor1.VCC, Espessif_Serial_Wifi_Modul_1.VCC, S5.pin3
  GND: Часть1.GND, Часть2.GND, M1.pin4, M1.pin5, Capacitive_Soil_Moisture_Sensor1.GND, Espessif_Serial_Wifi_Modul_1.GND, S5.pin2

notes:
  Parts List
  - Arduino Uno
  - 4 Buttons
  - GLCD 128x64
  - BME280
  - pH Sensor
  - Capacitive Soil Moisure Sensor
  - ADS1115
  - ESP-01
  - Light Sensor
  Buttons Order
  From left to right:
  Back, Down, Up, OK

custom parts:
  ph-4502c: ph-4502c PH Meter.
  ADS1115 16-bit ADC Breakout: ADS1015 12-bit I2C ADC+PGA Breakout
  ESP8266 ESP01: Generic WiFi Module based on the ESP8266 with onboard PCB antenna and UART communications
  LDR light sensor: Light sensor module. 3.3 V to 5V power.
